// Logisim project h.circ as structural Verilog: 1 circuit, main circuit main
module main (
  input  [3:0] in_1,
  input  [3:0] in_2,
  input  in_3
);

  wire and_1_out, and_2_out, and_3_out, and_4_out, and_5_out, clock_1_out, d_ff_1_qn, d_ff_2_qn, nand_1_out,
       nand_2_out, or_1_out, or_2_out, or_3_out, or_4_out;

  Clock clock_1 (.out(clock_1_out));
  nand nand_1 (nand_1_out, in_1[1], d_ff_1_qn, d_ff_2_qn);
  or or_1 (or_1_out, in_1[3], in_1[2], d_ff_1_qn, ~d_ff_2_qn);  // OR_Gate
  or or_2 (or_2_out, in_1[2], ~in_1[1], ~d_ff_1_qn, d_ff_2_qn);  // OR_Gate
  nand nand_2 (nand_2_out, in_1[3], ~in_1[1], d_ff_1_qn, d_ff_2_qn);  // NAND_Gate
  or or_3 (or_3_out, ~in_1[3], in_1[2], d_ff_1_qn, ~d_ff_2_qn);  // OR_Gate
  or or_4 (or_4_out, in_1[3], in_1[1], ~d_ff_1_qn, d_ff_2_qn);  // OR_Gate
  and and_1 (and_1_out, nand_1_out, or_1_out, or_2_out);
  and and_2 (and_2_out, nand_2_out, or_3_out, or_4_out);
  D_Flip_Flop d_ff_1 (
    .clk(clock_1_out), .D(and_1_out), .Qn(d_ff_1_qn), .preset(in_3), .en(in_3), .reset(in_3));  // open: Q
  D_Flip_Flop d_ff_2 (.clk(clock_1_out), .D(and_2_out), .Qn(d_ff_2_qn), .en(in_3));  // open: Q, preset, reset
  and and_3 (and_3_out, d_ff_2_qn, ~clock_1_out);  // AND_Gate
  LED led_1 (.in(and_3_out));
  and and_4 (and_4_out, ~d_ff_2_qn, d_ff_1_qn);  // AND_Gate
  LED led_2 (.in(and_4_out));
  LED led_3 (.in(and_5_out));
  and and_5 (and_5_out, d_ff_1_qn, d_ff_2_qn);

  assign in_1[0] = in_1[1];
  assign in_2 = {in_1[3:1], in_1[1]};
endmodule
