// Logisim project halimeowdumede23.circ as structural Verilog: 2 circuits, main circuit main
module main (
  input  in_1,
  input  in_2,
  input  in_3,
  output out_4,
  output out_5,
  output out_6,
  output g,
  output f,
  output a,
  output b,
  output out_11,
  output c,
  output e,
  output d,
  output out_15,
  output out_16,
  output g_2,
  output f_2,
  output a_2,
  output b_2,
  output c_2,
  output e_2,
  output d_2,
  output out_24,
  output out_25,
  output out_26,
  output g_3,
  output f_3,
  output a_3,
  output b_3,
  output c_3,
  output e_3,
  output d_3,
  output out_34,
  output out_35,
  output out_36,
  output g_4,
  output f_4,
  output a_4,
  output b_4,
  output c_4,
  output e_4,
  output d_4
);

  wire d_ff_1_qn, d_ff_2_q, d_ff_2_qn, d_ff_3_qn, d_ff_4_q, d_ff_4_qn, d_ff_5_qn, d_ff_6_q, d_ff_6_qn,
       d_ff_7_qn, d_ff_8_q, d_ff_8_qn, j_k_ff_1_q, j_k_ff_2_q, j_k_ff_2_qn, j_k_ff_3_q, j_k_ff_3_qn,
       j_k_ff_4_q, j_k_ff_4_qn, j_k_ff_5_q, j_k_ff_6_q, j_k_ff_6_qn, j_k_ff_7_q, j_k_ff_7_qn, j_k_ff_8_q,
       j_k_ff_8_qn, j_k_ff_9_q, j_k_ff_10_q, j_k_ff_10_qn, j_k_ff_11_q, j_k_ff_11_qn, j_k_ff_12_q,
       j_k_ff_12_qn, j_k_ff_13_q, j_k_ff_14_q, j_k_ff_14_qn, j_k_ff_15_q, j_k_ff_15_qn, j_k_ff_16_q,
       j_k_ff_16_qn;

  D_Flip_Flop d_ff_1 (.clk(in_1), .D(d_ff_1_qn), .Q(out_5), .Qn(d_ff_1_qn), .en(in_2));  // open: preset, reset
  D_Flip_Flop d_ff_2 (.clk(d_ff_1_qn), .D(d_ff_2_qn), .Q(d_ff_2_q), .Qn(d_ff_2_qn), .en(in_2));  // open: preset, reset
  D_Flip_Flop d_ff_3 (.clk(in_1), .D(d_ff_3_qn), .Q(out_15), .Qn(d_ff_3_qn), .en(in_2));  // open: preset, reset
  D_Flip_Flop d_ff_4 (.clk(d_ff_3_qn), .D(d_ff_4_qn), .Q(d_ff_4_q), .Qn(d_ff_4_qn), .en(in_2));  // open: preset, reset
  D_Flip_Flop d_ff_5 (.clk(in_1), .D(d_ff_5_qn), .Q(out_25), .Qn(d_ff_5_qn), .en(in_2));  // open: preset, reset
  D_Flip_Flop d_ff_6 (.clk(d_ff_5_qn), .D(d_ff_6_qn), .Q(d_ff_6_q), .Qn(d_ff_6_qn), .en(in_2));  // open: preset, reset
  D_Flip_Flop d_ff_7 (.clk(in_1), .D(d_ff_7_qn), .Q(out_35), .Qn(d_ff_7_qn), .en(in_2));  // open: preset, reset
  D_Flip_Flop d_ff_8 (.clk(d_ff_7_qn), .D(d_ff_8_qn), .Q(d_ff_8_q), .Qn(d_ff_8_qn), .en(in_2));  // open: preset, reset
  and and_1 (out_4, d_ff_1_qn, d_ff_2_qn);
  and and_2 (out_6, d_ff_1_qn, d_ff_2_q);
  and and_3 (out_11, d_ff_3_qn, d_ff_4_qn);
  and and_4 (out_16, d_ff_3_qn, d_ff_4_q);
  and and_5 (out_24, d_ff_5_qn, d_ff_6_qn);
  and and_6 (out_26, d_ff_5_qn, d_ff_6_q);
  and and_7 (out_34, d_ff_7_qn, d_ff_8_qn);
  and and_8 (out_36, d_ff_7_qn, d_ff_8_q);
  J_K_Flip_Flop j_k_ff_1 (.J(in_2), .clk(j_k_ff_2_qn), .K(in_2), .Q(j_k_ff_1_q));  // open: Qn, preset, en, reset
  J_K_Flip_Flop j_k_ff_2 (
    .J(in_2), .clk(j_k_ff_3_qn), .K(in_2), .Q(j_k_ff_2_q), .Qn(j_k_ff_2_qn));  // open: preset, en, reset
  J_K_Flip_Flop j_k_ff_3 (
    .J(in_2), .clk(j_k_ff_4_qn), .K(in_2), .Q(j_k_ff_3_q), .Qn(j_k_ff_3_qn));  // open: preset, en, reset
  J_K_Flip_Flop j_k_ff_4 (.J(in_2), .clk(in_1), .K(in_2), .Q(j_k_ff_4_q), .Qn(j_k_ff_4_qn));  // open: preset, en, reset
  J_K_Flip_Flop j_k_ff_5 (.J(in_2), .clk(j_k_ff_6_qn), .K(in_2), .Q(j_k_ff_5_q));  // open: Qn, preset, en, reset
  J_K_Flip_Flop j_k_ff_6 (
    .J(in_2), .clk(j_k_ff_7_qn), .K(in_2), .Q(j_k_ff_6_q), .Qn(j_k_ff_6_qn));  // open: preset, en, reset
  J_K_Flip_Flop j_k_ff_7 (
    .J(in_2), .clk(j_k_ff_8_qn), .K(in_2), .Q(j_k_ff_7_q), .Qn(j_k_ff_7_qn));  // open: preset, en, reset
  J_K_Flip_Flop j_k_ff_8 (.J(in_2), .clk(in_1), .K(in_2), .Q(j_k_ff_8_q), .Qn(j_k_ff_8_qn));  // open: preset, en, reset
  J_K_Flip_Flop j_k_ff_9 (.J(in_2), .clk(j_k_ff_10_qn), .K(in_2), .Q(j_k_ff_9_q));  // open: Qn, preset, en, reset
  J_K_Flip_Flop j_k_ff_10 (
    .J(in_2), .clk(j_k_ff_11_qn), .K(in_2), .Q(j_k_ff_10_q), .Qn(j_k_ff_10_qn));  // open: preset, en, reset
  J_K_Flip_Flop j_k_ff_11 (
    .J(in_2), .clk(j_k_ff_12_qn), .K(in_2), .Q(j_k_ff_11_q), .Qn(j_k_ff_11_qn));  // open: preset, en, reset
  J_K_Flip_Flop j_k_ff_12 (
    .J(in_2), .clk(in_1), .K(in_2), .Q(j_k_ff_12_q), .Qn(j_k_ff_12_qn));  // open: preset, en, reset
  J_K_Flip_Flop j_k_ff_13 (.J(in_2), .clk(j_k_ff_14_qn), .K(in_2), .Q(j_k_ff_13_q));  // open: Qn, preset, en, reset
  J_K_Flip_Flop j_k_ff_14 (
    .J(in_2), .clk(j_k_ff_15_qn), .K(in_2), .Q(j_k_ff_14_q), .Qn(j_k_ff_14_qn));  // open: preset, en, reset
  J_K_Flip_Flop j_k_ff_15 (
    .J(in_2), .clk(j_k_ff_16_qn), .K(in_2), .Q(j_k_ff_15_q), .Qn(j_k_ff_15_qn));  // open: preset, en, reset
  J_K_Flip_Flop j_k_ff_16 (
    .J(in_2), .clk(in_1), .K(in_2), .Q(j_k_ff_16_q), .Qn(j_k_ff_16_qn));  // open: preset, en, reset
  // _7_segment_display_driver 7_segment_display_driver_1: pin names not known; wires that end beside it: j_k_ff_1_q, j_k_ff_2_q, j_k_ff_3_q, j_k_ff_4_q, a, b, c, d, e, f, g
  // _7_segment_display_driver 7_segment_display_driver_2: pin names not known; wires that end beside it: j_k_ff_5_q, j_k_ff_6_q, j_k_ff_7_q, j_k_ff_8_q, a_2, b_2, c_2, d_2, e_2, f_2, g_2
  // _7_segment_display_driver 7_segment_display_driver_3: pin names not known; wires that end beside it: j_k_ff_9_q, j_k_ff_10_q, j_k_ff_11_q, j_k_ff_12_q, a_3, b_3, c_3, d_3, e_3, f_3, g_3
  // _7_segment_display_driver 7_segment_display_driver_4: pin names not known; wires that end beside it: j_k_ff_16_qn, j_k_ff_13_q, j_k_ff_14_q, j_k_ff_15_q, j_k_ff_16_q, a_4, b_4, c_4, d_4, e_4, f_4, g_4
endmodule

module a (
);

  main main_1 ();  // open: in_2, out_4, out_5, out_6, out_11, out_15, out_16, out_24, out_25, out_26, out_34, out_35, out_36, e, e_2, e_3, e_4, d, d_2, d_3, d_4, c, c_2, c_3, c_4, g, g_2, g_3, g_4, f, f_2, f_3, f_4, a, a_2, a_3, a_4, b, b_2, b_3, b_4, in_3, in_1
endmodule
