// Logisim project halimeowdumede233.circ as structural Verilog: 1 circuit, main circuit main
module main (
  input  Enable
);

  wire CLK_out, main_1_a, main_1_a_2, main_1_a_3, main_1_a_4, main_1_b, main_1_b_2, main_1_b_3, main_1_b_4,
       main_1_c, main_1_c_2, main_1_c_3, main_1_c_4, main_1_d, main_1_d_2, main_1_d_3, main_1_d_4, main_1_e,
       main_1_e_2, main_1_e_3, main_1_e_4, main_1_f, main_1_f_2, main_1_f_3, main_1_f_4, main_1_g,
       main_1_g_2, main_1_g_3, main_1_g_4, main_1_out_4, main_1_out_5, main_1_out_6, main_1_out_11,
       main_1_out_15, main_1_out_16, main_1_out_24, main_1_out_25, main_1_out_26, main_1_out_34,
       main_1_out_35, main_1_out_36, Reset_out;

  Clock CLK (.out(CLK_out));
  Button Reset (.out(Reset_out));
  LED Red (.in(main_1_out_24));
  LED Yellow (.in(main_1_out_25));
  LED Green (.in(main_1_out_26));
  _7_Segment_Display u_7_segment_display_1 (
    .g(main_1_g), .f(main_1_f_2), .a(main_1_a), .b(main_1_b_3), .e(main_1_e), .d(main_1_d), .c(main_1_c_4));  // open: dp
  _7_Segment_Display u_7_segment_display_2 (
    .g(main_1_g_2), .f(main_1_f_3), .a(main_1_a_3), .b(main_1_b_2), .e(main_1_e_2), .d(main_1_d_3),
    .c(main_1_c_3));  // open: dp
  _7_Segment_Display u_7_segment_display_3 (
    .g(main_1_g_3), .f(main_1_f), .a(main_1_a_2), .b(main_1_b_4), .e(main_1_e_3), .d(main_1_d_4), .c(main_1_c));  // open: dp
  LED Red_2 (.in(main_1_out_36));
  LED Yellow_2 (.in(main_1_out_35));
  LED Green_2 (.in(main_1_out_34));
  halimeowdumede23_main main_1 (
    .in_2(Enable), .out_4(main_1_out_4), .out_5(main_1_out_5), .out_6(main_1_out_6), .out_11(main_1_out_11),
    .out_15(main_1_out_15), .out_16(main_1_out_16), .out_24(main_1_out_24), .out_25(main_1_out_25),
    .out_26(main_1_out_26), .out_34(main_1_out_34), .out_35(main_1_out_35), .out_36(main_1_out_36),
    .e(main_1_e), .e_2(main_1_e_2), .e_3(main_1_e_3), .e_4(main_1_e_4), .d(main_1_d), .d_2(main_1_d_2),
    .d_3(main_1_d_3), .d_4(main_1_d_4), .c(main_1_c), .c_2(main_1_c_2), .c_3(main_1_c_3), .c_4(main_1_c_4),
    .g(main_1_g), .g_2(main_1_g_2), .g_3(main_1_g_3), .g_4(main_1_g_4), .f(main_1_f), .f_2(main_1_f_2),
    .f_3(main_1_f_3), .f_4(main_1_f_4), .a(main_1_a), .a_2(main_1_a_2), .a_3(main_1_a_3), .a_4(main_1_a_4),
    .b(main_1_b), .b_2(main_1_b_2), .b_3(main_1_b_3), .b_4(main_1_b_4), .in_3(Reset_out), .in_1(CLK_out));
  LED Red_3 (.in(main_1_out_4));
  LED Yellow_3 (.in(main_1_out_5));
  LED Green_3 (.in(main_1_out_6));
  _7_Segment_Display u_7_segment_display_4 (
    .g(main_1_g_4), .f(main_1_f_4), .a(main_1_a_4), .b(main_1_b), .e(main_1_e_4), .d(main_1_d_2),
    .c(main_1_c_2));  // open: dp
  LED Red_4 (.in(main_1_out_11));
  LED Yellow_4 (.in(main_1_out_15));
  LED Green_4 (.in(main_1_out_16));
endmodule
